// Logisim project NSC-8.circ as structural Verilog: 1 circuit, main circuit main
module main (
  input  [7:0] in_1,
  input  in_2,
  input  in_3,
  input  in_4,
  input  in_5,
  input  [3:0] in_6,
  input  in_7,
  input  [3:0] in_8,
  input  in_9,
  input  in_10,
  input  in_11,
  input  in_12,
  input  [3:0] in_13,
  input  in_14,
  input  in_15,
  input  [3:0] S3_LOW_NIB,
  input  [3:0] in_17,
  input  in_18,
  input  Setter,
  input  in_20
);

  wire adder_2_cout, and_1_out, and_2_out, and_3_out, and_4_out, and_5_out, and_6_out, and_7_out, and_8_out,
       and_9_out, and_10_out, and_11_out, and_12_out, and_13_out, and_14_out, and_15_out, and_16_out,
       and_17_out, and_18_out, and_19_out, and_20_out, and_21_out, and_22_out, and_23_out, and_24_out,
       and_25_out, and_26_out, and_27_out, and_28_out, and_29_out, and_30_out, and_31_out, and_32_out,
       and_33_out, and_34_out, and_35_out, and_36_out, and_37_out, and_38_out, and_39_out, and_40_out,
       and_41_out, and_42_out, and_43_out, and_44_out, and_45_out, and_46_out, and_47_out, and_48_out,
       and_49_out, and_50_out, and_51_out, and_52_out, and_54_out, and_55_out, and_56_out, and_57_out,
       CE_LOW, CLK_DECODE, clock_2_out, controlled_buffer_1_out, controlled_buffer_2_out,
       controlled_buffer_3_out, controlled_buffer_4_out, controlled_buffer_21_out, controlled_buffer_22_out,
       controlled_buffer_23_out, controlled_buffer_24_out, CP, EA, EI_LOW, EP, EU, HALT_LOW, j_k_ff_1_q,
       j_k_ff_2_q, j_k_ff_3_q, j_k_ff_4_q, j_k_ff_5_qn, j_k_ff_6_q, j_k_ff_7_qn, j_k_ff_8_q, j_k_ff_9_q,
       j_k_ff_9_qn, j_k_ff_10_q, j_k_ff_10_qn, j_k_ff_11_q, j_k_ff_12_q, j_k_ff_12_qn, j_k_ff_13_q,
       j_k_ff_14_q, j_k_ff_14_qn, JMP, LA_LOW, LB_LOW, LI_LOW, LIA, LIB, LM_LOW, LO_LOW, not_1_out,
       not_2_out, not_3_out, not_4_out, not_6_out, not_10_out, not_12_out, not_13_out, not_14_out,
       not_15_out, not_16_out, not_17_out, not_18_out, not_19_out, not_20_out, not_23_out, not_24_out,
       not_25_out, not_27_out, not_28_out, not_29_out, or_1_out, or_2_out, or_3_out, or_4_out, or_5_out,
       or_6_out, or_9_out, or_11_out, or_12_out, or_13_out, or_15_out, or_16_out, STA, SU, undriven,
       undriven_2, undriven_3, undriven_4, undriven_5, undriven_6, undriven_7, undriven_8;
  wire [3:0] adder_1_out, adder_2_out, controlled_buffer_8_out, controlled_buffer_9_out, multiplexer_4_out,
       multiplexer_10_out, multiplexer_12_out, ram_1_dout, ram_2_dout, ram_3_dout, register_1_q,
       register_2_q, register_3_q, register_4_q, register_5_q, register_6_q, register_7_q, register_8_q,
       register_9_q, xor_4_out, xor_8_out;

  not not_1 (not_1_out, register_1_q[3]);
  not not_2 (not_2_out, register_1_q[2]);
  not not_3 (not_3_out, register_1_q[1]);
  not not_4 (not_4_out, register_1_q[0]);
  RAM #(.addrWidth(4), .dataWidth(4)) ram_1 (
    .addr(in_8), .we(in_9), .oe(in_10), .clk(in_10), .din(in_13), .dout(ram_1_dout));
  and and_1 (and_1_out, not_1_out, not_2_out, not_3_out, not_4_out);
  and and_2 (and_2_out, not_1_out, not_2_out, not_3_out, register_1_q[0]);
  and and_3 (and_3_out, not_1_out, not_2_out, register_1_q[1], not_4_out);
  and and_4 (and_4_out, not_1_out, not_2_out, register_1_q[1], register_1_q[0]);
  and and_5 (and_5_out, not_1_out, register_1_q[2], not_3_out, not_4_out);
  and and_6 (and_6_out, not_1_out, register_1_q[2], not_3_out, register_1_q[0]);
  and and_7 (and_7_out, not_1_out, register_1_q[2], register_1_q[1], not_4_out);
  and and_8 (and_8_out, not_1_out, register_1_q[2], register_1_q[1], register_1_q[0]);
  and and_9 (and_9_out, register_1_q[3], register_1_q[2], register_1_q[1], not_4_out);
  and and_10 (and_10_out, register_1_q[3], register_1_q[2], register_1_q[1], register_1_q[0]);
  and and_11 (and_11_out, and_5_out, j_k_ff_10_q);
  and and_12 (and_12_out, and_1_out, j_k_ff_10_q);
  or or_1 (or_1_out, EP, and_11_out, and_12_out, and_13_out, and_14_out);
  not not_5 (LM_LOW, or_1_out);
  LED led_1 (.in(ram_1_dout[3]));
  LED led_2 (.in(ram_1_dout[2]));
  LED led_3 ();  // open: in
  LED led_4 ();  // open: in
  and and_13 (and_13_out, and_2_out, j_k_ff_10_q);
  J_K_Flip_Flop j_k_ff_1 (
    .J(not_6_out), .K(not_6_out), .clk(in_4), .Q(j_k_ff_1_q), .preset(undriven), .reset(undriven_2));  // open: Qn
  not not_6 (not_6_out, in_2);
  LED led_5 (.in(ram_1_dout[1]));
  LED led_6 (.in(ram_1_dout[0]));
  LED led_7 ();  // open: in
  LED led_8 ();  // open: in
  and and_14 (and_14_out, and_3_out, j_k_ff_10_q);
  and and_15 (and_15_out, and_1_out, j_k_ff_12_q);
  and and_16 (and_16_out, and_2_out, j_k_ff_12_q);
  or or_2 (or_2_out, j_k_ff_9_q, and_15_out, and_16_out, and_17_out);
  not not_7 (CE_LOW, or_2_out);
  and and_17 (and_17_out, and_3_out, j_k_ff_12_q);
  J_K_Flip_Flop j_k_ff_2 (
    .J(j_k_ff_1_q), .K(j_k_ff_1_q), .clk(in_4), .Q(j_k_ff_2_q), .preset(undriven_3), .reset(undriven_4));  // open: Qn
  and and_18 (and_18_out, and_1_out, j_k_ff_10_q);
  not not_8 (LI_LOW, j_k_ff_9_q);
  and and_19 (and_19_out, and_2_out, j_k_ff_10_q);
  and and_20 (and_20_out, and_3_out, j_k_ff_10_q);
  and and_21 (and_21_out, j_k_ff_1_q, j_k_ff_2_q);
  and and_22 (and_22_out, and_4_out, j_k_ff_10_q);
  J_K_Flip_Flop j_k_ff_3 (
    .J(and_21_out), .K(and_21_out), .clk(in_4), .Q(j_k_ff_3_q), .preset(undriven_5), .reset(undriven_6));  // open: Qn
  and and_23 (and_23_out, and_5_out, j_k_ff_10_q);
  or or_3 (or_3_out, and_18_out, and_19_out, and_20_out, and_22_out, and_23_out, and_25_out, and_26_out, and_27_out);
  not not_9 (EI_LOW, or_3_out);
  and and_24 (and_24_out, and_21_out, j_k_ff_3_q);
  and and_25 (and_25_out, and_6_out, j_k_ff_10_q);
  and and_26 (and_26_out, and_7_out, j_k_ff_10_q);
  J_K_Flip_Flop j_k_ff_4 (
    .J(and_24_out), .K(and_24_out), .clk(in_4), .Q(j_k_ff_4_q), .preset(undriven_7), .reset(undriven_8));  // open: Qn
  and and_27 (and_27_out, and_8_out, j_k_ff_10_q);
  Multiplexer multiplexer_1 (.in0(in_17[3]), .in1(controlled_buffer_4_out), .out(multiplexer_4_out[3]), .sel(STA));
  and and_28 (and_28_out, and_1_out, j_k_ff_12_q);
  or or_4 (or_4_out, in_12, STA);
  or or_5 (or_5_out, CLK_DECODE, in_15);
  not not_10 (not_10_out, CE_LOW);
  Multiplexer multiplexer_2 (.in0(in_17[2]), .in1(controlled_buffer_3_out), .out(multiplexer_4_out[2]), .sel(STA));
  and and_29 (and_29_out, and_6_out, j_k_ff_12_q);
  and and_30 (and_30_out, and_7_out, j_k_ff_12_q);
  or or_6 (or_6_out, and_28_out, and_29_out, and_30_out, and_31_out, and_32_out);
  not not_11 (LA_LOW, or_6_out);
  RAM #(.addrWidth(4), .asyncread("true"), .dataWidth(4)) ram_2 (
    .addr(multiplexer_12_out), .we(or_4_out), .oe(not_10_out), .clk(or_5_out), .din(multiplexer_4_out),
    .dout(ram_2_dout));
  Multiplexer multiplexer_3 (.in0(in_17[1]), .in1(controlled_buffer_2_out), .out(multiplexer_4_out[1]), .sel(STA));
  Clock clock_1 ();  // open: out
  and and_31 (and_31_out, and_2_out, j_k_ff_14_q);
  Multiplexer multiplexer_4 (.in0(in_17[0]), .in1(controlled_buffer_1_out), .out(multiplexer_4_out[0]), .sel(STA));
  and and_32 (and_32_out, and_3_out, j_k_ff_14_q);
  J_K_Flip_Flop #(.trigger("falling")) j_k_ff_5 (
    .J(j_k_ff_14_q), .K(j_k_ff_14_qn), .clk(CLK_DECODE), .Q(EP), .Qn(j_k_ff_5_qn), .preset(Setter),
    .reset(in_20));
  and and_33 (and_33_out, and_5_out, j_k_ff_12_q);
  and and_34 (and_34_out, and_9_out, j_k_ff_10_q);
  or or_7 (EA, and_33_out, and_34_out);
  and and_35 (and_35_out, JMP, controlled_buffer_9_out[0]);
  J_K_Flip_Flop #(.trigger("falling")) j_k_ff_6 (
    .J(not_12_out), .K(not_12_out), .clk(and_36_out), .Q(j_k_ff_6_q), .preset(and_35_out), .reset(and_38_out));  // open: Qn
  not not_12 (not_12_out, in_3);
  and and_36 (and_36_out, CLK_DECODE, CP);
  assign controlled_buffer_1_out = STA ? controlled_buffer_8_out[0] : 1'bz;  // Controlled_Buffer controlled_buffer_1
  assign controlled_buffer_2_out = STA ? controlled_buffer_8_out[1] : 1'bz;  // Controlled_Buffer controlled_buffer_2
  assign controlled_buffer_3_out = STA ? controlled_buffer_8_out[2] : 1'bz;  // Controlled_Buffer controlled_buffer_3
  assign controlled_buffer_4_out = STA ? controlled_buffer_8_out[3] : 1'bz;  // Controlled_Buffer controlled_buffer_4
  and and_37 (and_37_out, and_3_out, j_k_ff_14_q);
  or or_8 (SU, and_37_out, and_39_out);
  not not_13 (not_13_out, controlled_buffer_9_out[0]);
  and and_38 (and_38_out, JMP, not_13_out);
  not not_14 (not_14_out, CE_LOW);
  assign controlled_buffer_8_out[3] = not_14_out ? ram_2_dout[3] : 1'bz;  // Controlled_Buffer controlled_buffer_5
  assign controlled_buffer_8_out[2] = not_14_out ? ram_2_dout[2] : 1'bz;  // Controlled_Buffer controlled_buffer_6
  not not_15 (not_15_out, LI_LOW);
  not not_16 (not_16_out, EI_LOW);
  J_K_Flip_Flop #(.trigger("falling")) j_k_ff_7 (
    .J(EP), .K(j_k_ff_5_qn), .clk(CLK_DECODE), .Q(CP), .Qn(j_k_ff_7_qn));  // open: preset, reset
  and and_39 (and_39_out, and_7_out, j_k_ff_12_q);
  and and_40 (and_40_out, and_7_out, j_k_ff_12_q);
  not not_17 (not_17_out, in_7);
  assign controlled_buffer_8_out[1] = not_14_out ? ram_2_dout[1] : 1'bz;  // Controlled_Buffer controlled_buffer_7
  assign controlled_buffer_8_out[0] = not_14_out ? ram_2_dout[0] : 1'bz;  // Controlled_Buffer controlled_buffer_8
  or or_9 (or_9_out, in_18, CLK_DECODE);
  and and_41 (and_41_out, and_6_out, j_k_ff_12_q);
  and and_42 (and_42_out, JMP, controlled_buffer_9_out[1]);
  J_K_Flip_Flop #(.trigger("falling")) j_k_ff_8 (
    .J(j_k_ff_6_q), .K(j_k_ff_6_q), .clk(and_36_out), .Q(j_k_ff_8_q), .preset(and_42_out), .reset(and_44_out));  // open: Qn
  not not_18 (not_18_out, LM_LOW);
  Register #(.width(4)) register_1 (
    .D(controlled_buffer_8_out), .en(not_15_out), .clk(or_9_out), .Q(register_1_q));  // open: clr
  J_K_Flip_Flop #(.trigger("falling")) j_k_ff_9 (
    .J(CP), .K(j_k_ff_7_qn), .clk(CLK_DECODE), .Q(j_k_ff_9_q), .Qn(j_k_ff_9_qn));  // open: preset, reset
  and and_43 (and_43_out, and_2_out, j_k_ff_14_q);
  or or_10 (EU, and_40_out, and_41_out, and_43_out, and_45_out);
  not not_19 (not_19_out, controlled_buffer_9_out[1]);
  and and_44 (and_44_out, JMP, not_19_out);
  or or_11 (or_11_out, CLK_DECODE, in_5);
  Multiplexer multiplexer_5 (
    .in0(S3_LOW_NIB[3]), .in1(controlled_buffer_24_out), .out(multiplexer_10_out[3]), .sel(STA));
  J_K_Flip_Flop #(.trigger("falling")) j_k_ff_10 (
    .J(j_k_ff_9_q), .K(j_k_ff_9_qn), .clk(CLK_DECODE), .Q(j_k_ff_10_q), .Qn(j_k_ff_10_qn));  // open: preset, reset
  and and_45 (and_45_out, and_3_out, j_k_ff_14_q);
  and and_46 (and_46_out, and_2_out, j_k_ff_12_q);
  and and_47 (and_47_out, j_k_ff_6_q, j_k_ff_8_q);
  Multiplexer multiplexer_6 (.in0(in_6[3]), .in1(register_2_q[3]), .out(multiplexer_12_out[3]), .sel(not_17_out));
  not not_20 (not_20_out, CE_LOW);
  Multiplexer multiplexer_7 (
    .in0(S3_LOW_NIB[2]), .in1(controlled_buffer_23_out), .out(multiplexer_10_out[2]), .sel(STA));
  and and_48 (and_48_out, and_3_out, j_k_ff_12_q);
  or or_12 (or_12_out, and_46_out, and_48_out);
  not not_21 (LB_LOW, or_12_out);
  and and_49 (and_49_out, JMP, controlled_buffer_9_out[2]);
  J_K_Flip_Flop #(.trigger("falling")) j_k_ff_11 (
    .J(and_47_out), .K(and_47_out), .clk(and_36_out), .Q(j_k_ff_11_q), .preset(and_49_out), .reset(and_51_out));  // open: Qn
  Multiplexer multiplexer_8 (.in0(in_6[2]), .in1(register_2_q[2]), .out(multiplexer_12_out[2]), .sel(not_17_out));
  or or_13 (or_13_out, CLK_DECODE, in_14);
  Multiplexer multiplexer_9 (
    .in0(S3_LOW_NIB[1]), .in1(controlled_buffer_22_out), .out(multiplexer_10_out[1]), .sel(STA));
  J_K_Flip_Flop #(.trigger("falling")) j_k_ff_12 (
    .J(j_k_ff_10_q), .K(j_k_ff_10_qn), .clk(CLK_DECODE), .Q(j_k_ff_12_q), .Qn(j_k_ff_12_qn));  // open: preset, reset
  and and_50 (and_50_out, and_9_out, j_k_ff_10_q);
  not not_22 (LO_LOW, and_50_out);
  not not_23 (not_23_out, controlled_buffer_9_out[2]);
  and and_51 (and_51_out, JMP, not_23_out);
  and and_52 (and_52_out, and_47_out, j_k_ff_11_q);
  Register #(.width(4)) register_2 (
    .D(controlled_buffer_9_out), .en(not_18_out), .clk(or_11_out), .Q(register_2_q));  // open: clr
  RAM #(.addrWidth(4), .asyncread("true"), .dataWidth(4)) ram_3 (
    .addr(multiplexer_12_out), .we(or_4_out), .oe(not_20_out), .clk(or_13_out), .din(multiplexer_10_out),
    .dout(ram_3_dout));
  Multiplexer multiplexer_10 (
    .in0(S3_LOW_NIB[0]), .in1(controlled_buffer_21_out), .out(multiplexer_10_out[0]), .sel(STA));
  Register #(.width(4)) register_3 (
    .D(controlled_buffer_9_out), .en(not_15_out), .clk(or_9_out), .Q(register_3_q));  // open: clr
  and and_53 (LIA, and_4_out, j_k_ff_10_q);
  and and_54 (and_54_out, and_6_out, j_k_ff_10_q);
  and and_55 (and_55_out, JMP, controlled_buffer_9_out[3]);
  J_K_Flip_Flop #(.trigger("falling")) j_k_ff_13 (
    .J(and_52_out), .K(and_52_out), .clk(and_36_out), .Q(j_k_ff_13_q), .preset(and_55_out), .reset(and_57_out));  // open: Qn
  Multiplexer multiplexer_11 (.in0(in_6[1]), .in1(register_2_q[1]), .out(multiplexer_12_out[1]), .sel(not_17_out));
  J_K_Flip_Flop #(.trigger("falling")) j_k_ff_14 (
    .J(j_k_ff_12_q), .K(j_k_ff_12_qn), .clk(CLK_DECODE), .Q(j_k_ff_14_q), .Qn(j_k_ff_14_qn));  // open: preset, reset
  and and_56 (and_56_out, and_7_out, j_k_ff_10_q);
  or or_14 (LIB, and_54_out, and_56_out);
  not not_24 (not_24_out, controlled_buffer_9_out[3]);
  and and_57 (and_57_out, JMP, not_24_out);
  Multiplexer multiplexer_12 (.in0(in_6[0]), .in1(register_2_q[0]), .out(multiplexer_12_out[0]), .sel(not_17_out));
  assign controlled_buffer_9_out[0] = not_16_out ? register_3_q[0] : 1'bz;  // Controlled_Buffer controlled_buffer_9
  assign controlled_buffer_9_out[1] = not_16_out ? register_3_q[1] : 1'bz;  // Controlled_Buffer controlled_buffer_10
  assign controlled_buffer_9_out[2] = not_16_out ? register_3_q[2] : 1'bz;  // Controlled_Buffer controlled_buffer_11
  assign controlled_buffer_9_out[3] = not_16_out ? register_3_q[3] : 1'bz;  // Controlled_Buffer controlled_buffer_12
  and and_58 (STA, and_5_out, j_k_ff_12_q);
  assign controlled_buffer_9_out[0] = EP ? j_k_ff_6_q : 1'bz;  // Controlled_Buffer controlled_buffer_13
  assign controlled_buffer_9_out[1] = EP ? j_k_ff_8_q : 1'bz;  // Controlled_Buffer controlled_buffer_14
  assign controlled_buffer_9_out[2] = EP ? j_k_ff_11_q : 1'bz;  // Controlled_Buffer controlled_buffer_15
  assign controlled_buffer_9_out[3] = EP ? j_k_ff_13_q : 1'bz;  // Controlled_Buffer controlled_buffer_16
  assign controlled_buffer_9_out[0] = not_25_out ? ram_3_dout[0] : 1'bz;  // Controlled_Buffer controlled_buffer_17
  assign controlled_buffer_9_out[1] = not_25_out ? ram_3_dout[1] : 1'bz;  // Controlled_Buffer controlled_buffer_18
  assign controlled_buffer_9_out[2] = not_25_out ? ram_3_dout[2] : 1'bz;  // Controlled_Buffer controlled_buffer_19
  assign controlled_buffer_9_out[3] = not_25_out ? ram_3_dout[3] : 1'bz;  // Controlled_Buffer controlled_buffer_20
  not not_25 (not_25_out, CE_LOW);
  assign controlled_buffer_21_out = STA ? controlled_buffer_9_out[0] : 1'bz;  // Controlled_Buffer controlled_buffer_21
  assign controlled_buffer_22_out = STA ? controlled_buffer_9_out[1] : 1'bz;  // Controlled_Buffer controlled_buffer_22
  assign controlled_buffer_23_out = STA ? controlled_buffer_9_out[2] : 1'bz;  // Controlled_Buffer controlled_buffer_23
  assign controlled_buffer_24_out = STA ? controlled_buffer_9_out[3] : 1'bz;  // Controlled_Buffer controlled_buffer_24
  and and_59 (JMP, and_8_out, j_k_ff_10_q);
  not not_26 (HALT_LOW, and_10_out);
  Clock clock_2 (.out(clock_2_out));
  and and_60 (CLK_DECODE, clock_2_out, HALT_LOW);
  Clock clock_3 ();  // open: out
  Register #(.width(4)) register_4 (
    .D(controlled_buffer_8_out), .en(not_29_out), .clk(CLK_DECODE), .Q(register_4_q), .clr(LIA));
  assign controlled_buffer_9_out[3] = EA ? register_7_q[3] : 1'bz;  // Controlled_Buffer controlled_buffer_25
  assign controlled_buffer_9_out[2] = EA ? register_7_q[2] : 1'bz;  // Controlled_Buffer controlled_buffer_26
  assign controlled_buffer_9_out[1] = EA ? register_7_q[1] : 1'bz;  // Controlled_Buffer controlled_buffer_27
  assign controlled_buffer_9_out[0] = EA ? register_7_q[0] : 1'bz;  // Controlled_Buffer controlled_buffer_28
  assign controlled_buffer_8_out[3] = EA ? register_4_q[3] : 1'bz;  // Controlled_Buffer controlled_buffer_29
  assign controlled_buffer_8_out[2] = EA ? register_4_q[2] : 1'bz;  // Controlled_Buffer controlled_buffer_30
  assign controlled_buffer_8_out[1] = EA ? register_4_q[1] : 1'bz;  // Controlled_Buffer controlled_buffer_31
  assign controlled_buffer_8_out[0] = EA ? register_4_q[0] : 1'bz;  // Controlled_Buffer controlled_buffer_32
  assign controlled_buffer_9_out[0] = EU ? adder_2_out[0] : 1'bz;  // Controlled_Buffer controlled_buffer_33
  assign controlled_buffer_9_out[1] = EU ? adder_2_out[1] : 1'bz;  // Controlled_Buffer controlled_buffer_34
  assign controlled_buffer_9_out[2] = EU ? adder_2_out[2] : 1'bz;  // Controlled_Buffer controlled_buffer_35
  assign controlled_buffer_9_out[3] = EU ? adder_2_out[3] : 1'bz;  // Controlled_Buffer controlled_buffer_36
  assign controlled_buffer_8_out[3] = EU ? adder_1_out[3] : 1'bz;  // Controlled_Buffer controlled_buffer_37
  assign controlled_buffer_8_out[2] = EU ? adder_1_out[2] : 1'bz;  // Controlled_Buffer controlled_buffer_38
  assign controlled_buffer_8_out[1] = EU ? adder_1_out[1] : 1'bz;  // Controlled_Buffer controlled_buffer_39
  assign controlled_buffer_8_out[0] = EU ? adder_1_out[0] : 1'bz;  // Controlled_Buffer controlled_buffer_40
  Register #(.width(4)) register_5 (
    .D(controlled_buffer_8_out), .en(not_28_out), .clk(CLK_DECODE), .Q(register_5_q), .clr(LIB));
  Register #(.width(4)) register_6 (
    .D(controlled_buffer_8_out), .en(not_27_out), .clk(CLK_DECODE), .Q(register_6_q));  // open: clr
  xor xor_1 (xor_4_out[3], register_5_q[3], SU);
  xor xor_2 (xor_4_out[2], register_5_q[2], SU);
  xor xor_3 (xor_4_out[1], register_5_q[1], SU);
  xor xor_4 (xor_4_out[0], register_5_q[0], SU);
  LED led_9 (.in(register_6_q[3]));
  or or_15 (or_15_out, not_29_out, LIA);
  Adder #(.width(4)) adder_1 (.a(register_4_q), .b(xor_4_out), .out(adder_1_out), .cin(adder_2_cout));  // open: cout
  or or_16 (or_16_out, not_28_out, LIB);
  LED led_10 (.in(register_6_q[2]));
  LED led_11 (.in(register_6_q[1]));
  Register #(.width(4)) register_7 (
    .D(controlled_buffer_9_out), .en(or_15_out), .clk(CLK_DECODE), .Q(register_7_q));  // open: clr
  xor xor_5 (xor_8_out[3], register_8_q[3], SU);
  Register #(.width(4)) register_8 (
    .D(controlled_buffer_9_out), .en(or_16_out), .clk(CLK_DECODE), .Q(register_8_q));  // open: clr
  Register #(.width(4)) register_9 (
    .D(controlled_buffer_9_out), .en(not_27_out), .clk(CLK_DECODE), .Q(register_9_q));  // open: clr
  LED led_12 (.in(register_6_q[0]));
  LED led_13 (.in(register_9_q[3]));
  LED led_14 (.in(register_9_q[2]));
  Clock clock_4 ();  // open: out
  xor xor_6 (xor_8_out[2], register_8_q[2], SU);
  xor xor_7 (xor_8_out[1], register_8_q[1], SU);
  LED led_15 (.in(register_9_q[1]));
  LED led_16 (.in(register_9_q[0]));
  Adder #(.width(4)) adder_2 (.a(register_7_q), .b(xor_8_out), .out(adder_2_out), .cin(SU), .cout(adder_2_cout));
  xor xor_8 (xor_8_out[0], register_8_q[0], SU);
  not not_27 (not_27_out, LO_LOW);
  not not_28 (not_28_out, LB_LOW);
  not not_29 (not_29_out, LA_LOW);

  // Notes on the sheet:
  //   LDA (0000)
  //   ADD (0001)
  //   SUB (0010)
  //   LDAI (0011)
  //   STA (0100)
  //   ADDI (0101)
  //   SUBI (0110)
  //   JUMP (0111)
  //   OUT (1110)
  //   HLT (1111)
  //   CONTROL MATRIX
  //   STW(1)/manual(0)
  //   -CE
  //   S3 HI NIB
  //   STW
  //   Manual Write Enable
  //   RESetter
  //   CLK
  //   -LI
  //   -EI
  //   -LM
  //   CLK
  //   S1
  //   S2 RUN(0)/PROG(1)
  //   INSTRUCTION REGISTER
  //   CONTROLLER
  //   RING COUNTER
  //   PROGRAM COUNTER
  //   MAR
  //   RAM
  //   -CE
  //   Low Nibble
  //   High Nibble
  //   74LS126
  //   74LS126
  //   74LS126
  //   Low Nibble
  //   High Nibble
  //   Interactive Clock
  //   74LS126
  //   74LS173
  //   74LS173
  //   74LS173
  //   ACCUMULATOR A
  //   LOGIC UNIT
  //   B REGISTER
  //   Output Register
  //   74LS173
  //   74LS173
  //   74LS173
  //   LIA
  //   SU
  //   CLK
  //   LIB
  //   -LB
  //   EU
  //   -LO
endmodule
